# Fritzing sketch ENC26J60_hook_up (saved by Fritzing 0.9.3b)

parts:
  ENC28J1 = ENC28J60
  Componente1 = Arduino Uno (Rev3)

nets:
  5V: ENC28J1.5v, Componente1.5V
  N1: ENC28J1.INT, ENC28J1.SO, Componente1.D12/MISO, Componente1.D2
  N2: ENC28J1.SCK, ENC28J1.RST, Componente1.D13/SCK
  GND: ENC28J1.GND, Componente1.GND
  N3: ENC28J1.SI, Componente1.D11_PWM/MOSI
  N4: ENC28J1.CS, Componente1.D10_PWM/SS

custom parts:
  ENC28J60: Ethernet Module ENC28J60
