# Fritzing sketch RainSensor_hook_up (saved by Fritzing 0.9.3b)
breadboards: 1

parts:
  Componente1 = Arduino Uno (Rev3)
  YL-83_-_Control_Board1 = YL-83 Rain Sensor - Control Board
  YL-83_-_Detection_Board1 = YL-83 Rain Sensor - Detection Board

nets:
  N1: Componente1.A1, YL-83_-_Control_Board1.AO
  N2: Componente1.D6_PWM, YL-83_-_Control_Board1.DO
  5V: Componente1.5V, YL-83_-_Control_Board1.VCC
  GND: Componente1.GND, YL-83_-_Control_Board1.GND
  N3: YL-83_-_Control_Board1.POS, YL-83_-_Detection_Board1.NEG
  N4: YL-83_-_Control_Board1.NEG, YL-83_-_Detection_Board1.POS

custom parts:
  YL-83 Rain Sensor - Control Board: The YL-83 is a rain sensor that has more resistance when dry and less resistance when wet. The module runs at 5V.
  YL-83 Rain Sensor - Detection Board: The YL-83 is a rain sensor that has more resistance when dry and less resistance when wet. The module runs at 5V.
